# Fritzing sketch projeto-01 (saved by Fritzing 0.9.3b)
breadboards: 2

parts:
  U1 = POT [package=pot_alpha_rv16af-20]
  Componente1 = Arduino Uno (Rev3)
  U3 = LCD-16X2 [package=lcd-16x2]
  Componente2 = Bluetooth HC-05 Macho  # not connected

nets:
  5V: U1.A, Componente1.5V, U3.VDD, U3.A
  N1: U1.S, U3.VO
  GND: U1.E, Componente1.GND, U3.VSS, U3.R_W, U3.K
  N2: Componente1.D2, U3.RS
  N3: Componente1.D3_PWM, U3.E
  N4: Componente1.D4, U3.DB4
  N5: Componente1.D5_PWM, U3.DB5
  N6: Componente1.D6_PWM, U3.DB6
  N7: Componente1.D7, U3.DB7
