# Fritzing sketch projeto-02 (saved by Fritzing 0.9.3b)
breadboards: 1

parts:
  Componente1 = Arduino Uno (Rev3)
  Componente2 = Bluetooth HC-05 Macho
  LED1 = RGB LED (com. cathode, rgb) [package="5 mm [THT]"]
  R1 = Resistor [tolerance=±5% resistance=220 package="2512 [SMD]"]
  R2 = Resistor [tolerance=±5% resistance=220 package="2512 [SMD]"]
  R3 = Resistor [tolerance=±5% resistance=220 package="2512 [SMD]"]

nets:
  N1: Componente1.D9_PWM, R3.Pin_0
  N2: Componente1.D10_PWM/SS, R2.Pin_0
  N3: Componente1.D11_PWM/MOSI, R1.Pin_0
  N4: Componente1.D0/RX, Componente2.TXD
  N5: Componente1.D1/TX, Componente2.RXD
  5V: Componente1.5V, Componente2.VCC
  GND: Componente1.GND, Componente2.GND, LED1.common_cathode
  N6: LED1.red_anode, R1.Pin_1
  N7: LED1.green_anode, R2.Pin_1
  N8: LED1.blue_anode, R3.Pin_1
