# Fritzing sketch projeto-03 (saved by Fritzing 0.9.3b)
breadboards: 1

parts:
  Componente1 = Arduino Uno (Rev3)
  R1 = Resistor [tolerance=±5% resistance=220 package=THT]
  LED1 = smd LED [color="Red (633nm)" package="0603 [SMD]"]
  Componente2 = RFID-RC522 [part_number=101218]

nets:
  N1: Componente1.D8, R1.Pin_0
  N2: Componente1.D9_PWM, Componente2.RST
  N3: Componente1.D10_PWM/SS, Componente2.SDA
  N4: Componente1.D11_PWM/MOSI, Componente2.MOSI
  N5: Componente1.D12/MISO, Componente2.MISO
  N6: Componente1.D13/SCK, Componente2.SCK
  3V3: Componente1.3V3, Componente2.3.3V
  GND: Componente1.GND, LED1.cathode, Componente2.GND
  N7: R1.Pin_1, LED1.anode
