# Fritzing sketch projeto-04-alerta (saved by Fritzing 0.9.3b)
breadboards: 1

parts:
  U1 = NodeMCU V1.0
  hc-sr1 = hc-sr04
  YwRobot_Power_Supply1 = YwRobot Breadboard Power Supply [part_number=545043]
  U2 = NodeMCU V1.0

nets:
  N1: U1.D2, U2.D0
  N2: U1.D3, hc-sr1.Trig, U2.D1
  N3: U1.D4, hc-sr1.Echo, U2.D2
  N4: U1.3V3, U2.D3, U2.TX, U2.CLK
  N5: U1.GND, U2.D4, U2.RX, U2.EN, U2.SD0
  N6: U1.D5, U1.RST, U2.3V3
  N7: U1.D6, U1.EN, U2.GND
  N8: U1.D7, U2.D5
  N9: U1.D8, U2.D6
  N10: U1.RX, U2.D7
  N11: U1.TX, U2.D8
  N12: U1.Vin, U2.RST
  N13: U1.CLK, U2.CMD
  N14: U1.SD0, U2.SD1
  N15: U1.CMD, U2.SD2
  N16: U1.SD1, U2.SD3
  N17: U1.SD2, U2.RSV#40
  N18: U1.SD3, U2.RSV#41
  N19: U1.RSV#40, U2.A0
  N20: YwRobot_Power_Supply1.VCC#5, YwRobot_Power_Supply1.VCC#6
  N21: YwRobot_Power_Supply1.VCC#9, YwRobot_Power_Supply1.VCC#10
  N22: YwRobot_Power_Supply1.GND#11, YwRobot_Power_Supply1.GND#12
  N23: YwRobot_Power_Supply1.GND#13, YwRobot_Power_Supply1.GND#14

custom parts:
  NodeMCU V1.0: ESP8266 based NodeMCU
  YwRobot Breadboard Power Supply: The YwRobot Breadboard Power Supply (MB-V2) has two power rails; they can be 5V or 3V3. Power to the module can be provided through the female USB socket or through the A10 (female) 2.1mm power jack.
