# Fritzing sketch projeto-04-led (saved by Fritzing 0.9.3b)
breadboards: 1

parts:
  R1 = Resistor [tolerance=±5% resistance=220 package=THT]
  LED1 = smd LED [color="Red (633nm)" package="0603 [SMD]"]
  U1 = NodeMCU V1.0

nets:
  N1: R1.Pin_0, U1.D7
  N2: R1.Pin_1, LED1.anode
  N3: LED1.cathode, U1.GND

custom parts:
  NodeMCU V1.0: ESP8266 based NodeMCU
