# Fritzing sketch projeto-05 (saved by Fritzing 0.9.3b)
breadboards: 1

parts:
  U1 = NodeMCU V1.0
  DHT3 = DHT11 Humitidy and Temperature Sensor

nets:
  N1: U1.D3, DHT3.DATA
  GND: U1.GND, DHT3.GND
  VIN: U1.Vin, DHT3.VDD

custom parts:
  NodeMCU V1.0: ESP8266 based NodeMCU
  DHT11 Humitidy and Temperature Sensor: DHT11 Humidity and Temperature Sensor
